# Fritzing sketch hardwareConfig (saved by Fritzing 0.9.3b)

parts:
  U1 = LCD-16X2 [package=lcd-16x2]
  U2 = POT_SWITCH [package=pot_pth]
  Raspberry_Pi_1 = Raspberry Pi 3 [part_number=RPI-3-V1.2]
  S1 = Round Pushbutton
  Q1 = PNP-Transistor [package="TO92 [THT]"]
  BAT1 = BC9VPC [package=bc9vpc]

nets:
  GND: U1.VSS, U1.R_W, U1.K, U2.G$1_A, Raspberry_Pi_1.GND, S1.leg1, Q1.GND, BAT1.V-
  VDD: U1.VDD, U1.A, U2.G$1_E, Raspberry_Pi_1.5V
  N1: U1.VO, U2.G$2_1
  N2: U1.RS, Raspberry_Pi_1.GIPO7
  N3: U1.E, Raspberry_Pi_1.GIPO8
  N4: U1.DB4, Raspberry_Pi_1.GIPO25
  N5: U1.DB5, Raspberry_Pi_1.GIPO24
  N6: U1.DB6, Raspberry_Pi_1.GIPO23
  N7: U1.DB7, Raspberry_Pi_1.GIPO18
  N8: Raspberry_Pi_1.GPIO2, Q1.INPUT
  N9: Raspberry_Pi_1.GIPO26, S1.leg0
  N10: Q1.12V, BAT1.V+

custom parts:
  PNP-Transistor: A standard PNP signal transistor
